// Logisim project faerie.circ as structural Verilog: 2 circuits, main circuit main
module main (
  output out_1,
  output out_2,
  output out_3,
  output out_4
);

  wire alu_1_cout, and_1_out, and_2_out, and_3_out, and_7_out, and_8_out, and_9_out, and_10_out, and_11_out,
       and_12_out, CF_q, comparator_1_eq, demultiplexer_1_out1, multiplexer_2_out, nand_1_out, nor_1_out,
       nor_2_out, not_1_out, not_2_out, or_1_out, or_2_out, or_4_out, or_6_out, or_7_out, or_8_out,
       or_10_out, xor_3_out, ZF_q;
  wire [0:0] AL_q;
  wire [1:0] IR_q, IR_q_2;
  wire [3:0] IR_q_3;
  wire [7:0] A_q, AH_q, alu_1_q, and_5_out, B_q, bit_extender_1_out, controlled_buffer_1_out, FSM_q;
  wire [13:0] bit_extender_2_out;
  wire [14:0] bit_extender_3_out;
  wire [15:0] multiplexer_1_out, or_9_out, PC_q, xor_1_out, xor_2_out;

  Register FSM (
    .D(and_5_out), .Q({FSM_q[7], out_3, FSM_q[5:3], and_5_out[3], FSM_q[1:0]}), .clk(out_1), .clr(out_2));  // open: en
  nor nor_1 (nor_1_out, FSM_q[0], FSM_q[1], and_5_out[3], FSM_q[3], FSM_q[4], FSM_q[5], out_3, FSM_q[7]);
  or or_1 (or_1_out, FSM_q[4], or_2_out);
  or or_2 (or_2_out, nor_1_out, FSM_q[0], and_1_out, FSM_q[1]);
  and and_1 (and_1_out, FSM_q[4], IR_q[0], IR_q[1]);
  or or_3 (out_4, or_1_out, and_5_out[3], FSM_q[3]);
  and and_2 (and_2_out, nor_1_out, not_1_out);
  and and_3 (and_3_out, FSM_q[0], nor_2_out);
  not not_1 (not_1_out, nand_1_out);
  and and_4 (and_5_out[1], FSM_q[0], IR_q[1]);
  or or_4 (or_4_out, FSM_q[3], FSM_q[1], and_2_out, and_3_out);
  Demultiplexer #(.select(2), .enable("false")) demultiplexer_1 (
    .out0(and_5_out[4]), .out1(demultiplexer_1_out1), .out2(and_5_out[6]), .out3(and_5_out[7]),
    .in(or_4_out), .sel(IR_q_2));
  nor nor_2 (nor_2_out, IR_q[0], IR_q[1]);
  nand nand_1 (nand_1_out, controlled_buffer_1_out[0], controlled_buffer_1_out[1]);
  and and_5 (and_5_out[0], nand_1_out, nor_1_out);
  and and_6 (and_5_out[2], FSM_q[0], IR_q[0]);
  or or_5 (and_5_out[5], FSM_q[4], demultiplexer_1_out1);
  or or_6 (or_6_out, FSM_q[1], and_5_out[3]);
  or or_7 (or_7_out, FSM_q[3], FSM_q[0]);
  and and_7 (and_7_out, FSM_q[7], or_10_out);
  Clock clock_1 (.out(out_1));
  Button RESET (.out(out_2));
  assign xor_1_out = 16'hc000 ^ PC_q;  // XOR_Gate xor_1, 16 bits wide
  assign xor_2_out = 16'hc000 ^ or_9_out;  // XOR_Gate xor_2, 16 bits wide
  Counter #(.width(16), .max('hffff)) PC (
    .load(and_7_out), .D(xor_2_out), .count(or_2_out), .Q(PC_q), .clk(out_1), .clr(out_2));  // open: carry
  Register AH (.D(controlled_buffer_1_out), .en(or_6_out), .Q(AH_q), .clk(out_1));  // open: clr
  Register AL (.D(controlled_buffer_1_out), .en(or_7_out), .Q({or_9_out[7:1], AL_q[0]}), .clk(out_1));  // open: clr
  Register IR (.D(controlled_buffer_1_out), .en(nor_1_out), .Q({IR_q_3, IR_q_2, IR_q}), .clk(out_1));  // open: clr
  assign bit_extender_1_out = {{7{or_8_out}}, or_8_out};  // Bit_Extender bit_extender_1
  or or_8 (or_8_out, FSM_q[3], and_5_out[3]);
  Multiplexer #(.width(16), .enable("false")) multiplexer_1 (
    .in0(or_9_out), .in1(xor_1_out), .out(multiplexer_1_out), .sel(or_2_out));
  or or_9 (or_9_out[0], and_5_out[3], AL_q[0]);
  assign or_9_out[15:8] = ~(bit_extender_1_out | ~AH_q);  // NOR_Gate nor_3, 8 bits wide
  // Probe on multiplexer_1_out
  // Probe on controlled_buffer_1_out
  assign controlled_buffer_1_out = out_3 ? A_q : 8'bz;  // Controlled_Buffer controlled_buffer_1
  Bit_Extender #(.in_width(16), .out_width(14)) bit_extender_2 (.in(multiplexer_1_out), .out(bit_extender_2_out));
  and and_8 (and_8_out, out_4, multiplexer_1_out[14], multiplexer_1_out[15]);
  Bit_Extender #(.in_width(16), .out_width(15)) bit_extender_3 (.in(multiplexer_1_out), .out(bit_extender_3_out));
  not not_2 (not_2_out, multiplexer_1_out[15]);
  Register A (.D(alu_1_q), .en(FSM_q[5]), .Q(A_q), .clk(out_1), .clr(out_2));
  Register B (.D(controlled_buffer_1_out), .en(FSM_q[4]), .Q(B_q), .clk(out_1), .clr(nor_1_out));
  and and_9 (and_9_out, not_2_out, out_3);
  and and_10 (and_10_out, not_2_out, out_4);
  ALU alu_1 (
    .Cin(CF_q), .A(A_q), .B(B_q), .Cout(alu_1_cout), .Q(alu_1_q), .CC(IR_q_3[3]), .SUB_AND(IR_q_3[2]),
    .SHL_XOR(IR_q_3[1]), .LOGIC_B(IR_q_3[0]));
  Register #(.width(1)) CF (.D(alu_1_cout), .en(FSM_q[5]), .Q(CF_q), .clk(out_1), .clr(out_2));
  and and_11 (and_11_out, ~ZF_q, ~CF_q);  // AND_Gate
  ROM #(.addrWidth(14)) rom_1 (.addr(bit_extender_2_out), .data(controlled_buffer_1_out), .sel(and_8_out));
  RAM #(.addrWidth(15), .bus("separate")) ram_1 (
    .addr(bit_extender_3_out), .din(controlled_buffer_1_out), .data(controlled_buffer_1_out),
    .str(and_9_out), .clk(out_1), .ld(and_10_out));  // open: sel, clr
  Comparator comparator_1 (.a(alu_1_q), .b({8{1'b0}}), .eq(comparator_1_eq));  // open: gt, lt
  and and_12 (and_12_out, CF_q, ~ZF_q);  // AND_Gate
  Register #(.width(1)) ZF (.D(comparator_1_eq), .en(FSM_q[5]), .Q(ZF_q), .clk(out_1), .clr(out_2));
  Multiplexer #(.select(2), .enable("false")) multiplexer_2 (
    .in0(ZF_q), .in1(CF_q), .in2(and_12_out), .in3(and_11_out), .out(multiplexer_2_out), .sel(IR_q_3[1:0]));
  xor xor_3 (xor_3_out, multiplexer_2_out, IR_q_3[2]);
  or or_10 (or_10_out, xor_3_out, IR_q_3[3]);

  // Notes on the sheet:
  //   Insn load
  //   Addr #1
  //   Addr #2
  //   Ptr #1
  //   Ptr #2
  //   Mem load
  //   ALU
  //   Mem store
  //   Branch
  //   contents of rom_1 (hex, n*v repeats v):
  //   59 2 2812*0 66
endmodule

module ALU (
  input  CC,
  input  Cin,
  input  [7:0] A,
  input  [7:0] B,
  input  SUB_AND,
  input  SHL_XOR,
  input  LOGIC_B,
  output Cout,
  output [7:0] Q
);

  wire adder_1_cout, multiplexer_1_out, not_1_out, or_1_out;
  wire [7:0] adder_1_out, bit_extender_1_out, bit_extender_2_out, multiplexer_2_out, multiplexer_3_out,
       multiplexer_5_out, multiplexer_7_out, nor_1_out, xor_1_out, xor_2_out, xor_3_out;
  wire [7:7] and_1_out;

  and and_1 (and_1_out[7], CC, Cin);
  Multiplexer #(.enable("false")) multiplexer_1 (.in0(SUB_AND), .in1(Cin), .out(multiplexer_1_out), .sel(CC));
  not not_1 (not_1_out, SUB_AND);
  Multiplexer #(.width(8), .enable("false")) multiplexer_2 (
    .in0(A), .in1(bit_extender_1_out), .out(multiplexer_2_out), .sel(SHL_XOR));
  assign bit_extender_1_out = {{7{SUB_AND}}, SUB_AND};  // Bit_Extender bit_extender_1
  assign xor_1_out = B ^ multiplexer_2_out;  // XOR_Gate xor_1, 8 bits wide
  assign xor_2_out = A ^ bit_extender_1_out;  // XOR_Gate xor_2, 8 bits wide
  assign bit_extender_2_out = {{7{not_1_out}}, not_1_out};  // Bit_Extender bit_extender_2
  Adder adder_1 (.a(A), .b(xor_1_out), .out(adder_1_out), .cin(multiplexer_1_out), .cout(adder_1_cout));
  assign nor_1_out = ~(xor_1_out | xor_2_out);  // NOR_Gate nor_1, 8 bits wide
  assign xor_3_out = nor_1_out ^ bit_extender_2_out;  // XOR_Gate xor_3, 8 bits wide
  or or_1 (or_1_out, SHL_XOR, not_1_out);
  Multiplexer #(.width(8), .enable("false")) multiplexer_3 (
    .in0(xor_1_out), .in1(xor_3_out), .out(multiplexer_3_out), .sel(SHL_XOR));
  Multiplexer #(.enable("false")) multiplexer_4 (.in0(A[0]), .in1(adder_1_cout), .out(Cout), .sel(or_1_out));
  Multiplexer #(.width(8), .enable("false")) multiplexer_5 (
    .in0({and_1_out[7], A[7:1]}), .in1(B), .out(multiplexer_5_out), .sel(LOGIC_B));
  Multiplexer #(.width(8), .enable("false")) multiplexer_6 (
    .in0(multiplexer_5_out), .in1(multiplexer_7_out), .out(Q), .sel(or_1_out));
  Multiplexer #(.width(8), .enable("false")) multiplexer_7 (
    .in0(adder_1_out), .in1(multiplexer_3_out), .out(multiplexer_7_out), .sel(LOGIC_B));

  // Notes on the sheet:
  //   SUB_AND: pull=down
  //   LOGIC_B: pull=down
  //   A: pull=down
  //   B: pull=down
  //   CC: pull=down
  //   Cin: pull=down
  //   SHL_XOR: pull=down
endmodule
